// Logisim project Sum-of-product.circ as structural Verilog: 1 circuit, main circuit main
module main (
  input  A,
  input  B,
  output X
);

  wire and_1_out, and_2_out;

  and and_1 (and_1_out, A, B);
  and and_2 (and_2_out, A, ~B);  // AND_Gate
  or or_1 (X, and_1_out, and_2_out);

  // Notes on the sheet:
  //   Kieran O'Connor
endmodule
