// Logisim project Traffic Light.circ as structural Verilog
module Traffic_Light (
  input  Clock,
  input  TA,
  input  TB,
  output Lights,
  output _01___Yellow,
  output out_6,
  output out_7
);

  wire and_1_out, and_2_out, d_ff_2_q, or_1_out, xor_1_out;

  and and_1 (and_1_out, ~Lights, ~d_ff_2_q, ~TA);  // AND_Gate
  and and_2 (and_2_out, Lights, ~d_ff_2_q, ~TB);  // AND_Gate
  xor xor_1 (xor_1_out, Lights, d_ff_2_q);
  or or_1 (or_1_out, and_1_out, and_2_out);
  D_Flip_Flop d_ff_1 (.clk(Clock), .D(xor_1_out), .Q(Lights));  // open: Qn, preset, en, reset
  D_Flip_Flop d_ff_2 (.clk(Clock), .D(or_1_out), .Q(d_ff_2_q));  // open: Qn, preset, en, reset
  and and_3 (_01___Yellow, ~Lights, d_ff_2_q);  // AND_Gate
  not not_1 (out_6, Lights);
  and and_4 (out_7, Lights, d_ff_2_q);

  // Notes on the sheet:
  //   Kieran O'Connor
  //   00 - Green
  //   10 - Red
endmodule

module FSM (
  input  Kieran_O_prime_Connor,
  input  in_2
);

  wire and_1_out, and_2_out, and_3_out, and_4_out, d_ff_1_q, d_ff_2_q, not_1_out, or_1_out;

  and and_1 (and_1_out, Kieran_O_prime_Connor, ~d_ff_1_q, ~d_ff_2_q);  // AND_Gate
  and and_2 (and_2_out, ~Kieran_O_prime_Connor, ~d_ff_1_q, d_ff_2_q);  // AND_Gate
  and and_3 (and_3_out, Kieran_O_prime_Connor, d_ff_1_q, d_ff_2_q);
  and and_4 (and_4_out, ~Kieran_O_prime_Connor, d_ff_1_q, ~d_ff_2_q);  // AND_Gate
  or or_1 (or_1_out, and_1_out, and_2_out, and_3_out, and_4_out);
  not not_1 (not_1_out, d_ff_2_q);
  D_Flip_Flop d_ff_1 (.clk(in_2), .D(or_1_out), .Q(d_ff_1_q));  // open: Qn, preset, en, reset
  D_Flip_Flop d_ff_2 (.clk(in_2), .D(not_1_out), .Q(d_ff_2_q));  // open: Qn, preset, en, reset
endmodule
