// Logisim project adder.circ as structural Verilog: 4 circuits, main circuit main
module main (
  input  in_1,
  input  in_2,
  input  in_3,
  input  in_4,
  input  in_5,
  input  in_6,
  input  in_7,
  input  in_8,
  output out_9,
  output out_10,
  output out_11,
  output out_12
);

  wire full_adder_2_c, full_adder_3_c, half_adder_1_out_4;

  full_adder full_adder_1 (.S(out_9), .A(in_2), .B(in_7), .Cin(full_adder_2_c));  // open: C
  full_adder full_adder_2 (.C(full_adder_2_c), .S(out_10), .A(in_1), .B(in_5), .Cin(full_adder_3_c));
  full_adder full_adder_3 (.C(full_adder_3_c), .S(out_11), .A(in_3), .B(in_8), .Cin(half_adder_1_out_4));
  half_adder half_adder_1 (.A(in_4), .B(in_6), .out_3(out_12), .out_4(half_adder_1_out_4));

  // Notes on the sheet:
  //   Kieran O'Connor
endmodule

module half_adder (
  input  A,
  input  B,
  output out_3,
  output out_4
);

  or or_1 (out_3, A, A, B);
  and and_1 (out_4, A, B);
endmodule

module full_adder (
  input  A,
  input  B,
  input  Cin,
  output C,
  output S
);

  wire and_1_out, and_2_out, and_3_out, or_1_out;

  and and_1 (and_1_out, A, B);
  and and_2 (and_2_out, B, Cin);
  and and_3 (and_3_out, A, Cin);
  or or_1 (or_1_out, A, B);
  or or_2 (C, and_1_out, and_2_out, and_3_out);
  or or_3 (S, or_1_out, Cin);
endmodule

module multi_bit_adder (
  input  in_1,
  input  in_2,
  input  in_3,
  input  in_4,
  input  in_5,
  input  in_6,
  input  in_7,
  input  in_8,
  output out_9,
  output out_10,
  output out_11,
  output out_12
);

  wire full_adder_2_c, full_adder_3_c, half_adder_1_out_4;

  full_adder full_adder_1 (.S(out_9), .A(in_2), .B(in_7), .Cin(full_adder_2_c));  // open: C
  full_adder full_adder_2 (.C(full_adder_2_c), .S(out_10), .A(in_1), .B(in_5), .Cin(full_adder_3_c));
  full_adder full_adder_3 (.C(full_adder_3_c), .S(out_11), .A(in_3), .B(in_8), .Cin(half_adder_1_out_4));
  half_adder half_adder_1 (.A(in_4), .B(in_6), .out_3(out_12), .out_4(half_adder_1_out_4));
endmodule
